# Fritzing sketch Circuit (saved by Fritzing 0.8.7b)
breadboards: 1

parts:
  Part1 = Arduino Pro
  Unlock = SWITCH-MOMENTARY-2 [package=tactile-switch-1101ne]
  Lock = SWITCH-MOMENTARY-2 [package=tactile-switch-1101ne]
  Buzz = SWITCH-MOMENTARY-2 [package=tactile-switch-1101ne]
  LED1 = LED - 5mm [color="Red (633nm)" package="5 mm [THT]"]
  Q1 = TRANSISTOR_NPN [package=to-92-ammo]
  R2 = Resistor [tolerance=±5% resistance=10k package=THT]
  R1 = Resistor [tolerance=±5% resistance=10k package=THT]
  J1 = Basic Servo
  R3 = Resistor [package="2512 [SMD]"]
  Buzzer = Buzzer 12mm [package=buzzer-ccv]

nets:
  N1: Part1.D4/A6, R3.Pin_1
  N2: Part1.D6_PWM, Lock.1, R1.Pin_1
  N3: Part1.D8, J1.pulse
  N4: Part1.D10_PWM/SS, Unlock.1, R2.Pin_1
  N5: Part1.D13/SCK, Q1.B
  GND: Part1.GND, Buzz.1, LED1.cathode, Q1.E, R2.Pin_0, R1.Pin_0, J1.gnd, Buzzer.1
  VCC: Part1.VCC, Unlock.2, Lock.2, J1.vcc
  N6: Buzz.2, Q1.C, Buzzer.2
  N7: LED1.anode, R3.Pin_0
