# Fritzing sketch outlet (saved by Fritzing 0.8.7b)
breadboards: 1

parts:
  U1 = Spark Core (v1.0)
  Q1 = TRANSISTOR_NPN [package=to-92]
  Q2 = TRANSISTOR_NPN [package=to-92]
  V1 = DC Power [voltage=5]
  Light = RELAY [package=relay-t9a]
  AC = RELAY [package=relay-t9a]

nets:
  N1: U1.A2, U1.3V3
  N2: U1.A3, U1.A6
  N3: U1.A5, U1.VIN
  N4: U1.GND, V1.V-, Light.COIL1, AC.COIL1
  N5: U1.D0, Q2.B
  N6: U1.D1, Q1.B
  N7: Q1.E, Q2.E, V1.V+
  N8: Q1.C, AC.COIL2
  N9: Q2.C, Light.COIL2

custom parts:
  Spark Core (v1.0): The Spark Core is a tiny Wi-Fi development board that makes it easy to create internet-connected hardware. The Core is all you need to get started; power it over USB and in minutes you'll be controlling LEDs, switches and motors and collecting data from sensors over the internet! It has 8 digital I/O pins, 8 analog I/O pins, 8 PWM pins; UART (Serial), SPI, I2C, and JTAG peripherals available.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
